// Logisim project 1 - Circuito Somador.circ as structural Verilog: 1 circuit, main circuit main
module main (
  input  in_1,
  input  A1,
  input  B1,
  input  A2,
  input  B2,
  output out_6,
  output out_7,
  output Overflow
);

  wire and_1_out, and_2_out, and_3_out, and_4_out, C_Out_out, xor_1_out, xor_2_out;

  xor xor_1 (xor_1_out, A1, B1);
  and and_1 (and_1_out, A1, B1);
  xor xor_2 (xor_2_out, A2, B2);
  and and_2 (and_2_out, A2, B2);
  xor xor_3 (out_6, in_1, xor_1_out);
  and and_3 (and_3_out, in_1, xor_1_out);
  xor xor_4 (out_7, C_Out_out, xor_2_out);
  and and_4 (and_4_out, C_Out_out, xor_2_out);
  or C_Out (C_Out_out, and_3_out, and_1_out);
  or C_Out_2 (Overflow, and_4_out, and_2_out);

  // Notes on the sheet:
  //   A leitura do resultado é feita de baixo para cima
  //   EQUAÇÃO MATEMÁTICA$$   a2 a1$+b2 b1$__________
endmodule
