// Logisim project 1 - Somador CLA (Carry Lookahead).circ as structural Verilog: 1 circuit, main circuit main
module main (
  input  A4,
  input  A3,
  input  A2,
  input  A1,
  input  B4,
  input  B3,
  input  B2,
  input  B1,
  output A3___B3,
  output A4___B4,
  output Carry_Out,
  output Carry_In,
  output A1___B1,
  output A2___B2
);

  wire displaydecoder_1_p1, displaydecoder_1_p3, displaydecoder_1_p4, displaydecoder_1_p6,
       displaydecoder_1_p7, displaydecoder_1_p9, displaydecoder_1_p10, displaydecoder_2_p1,
       displaydecoder_2_p3, displaydecoder_2_p4, displaydecoder_2_p6, displaydecoder_2_p7,
       displaydecoder_2_p9, displaydecoder_2_p10, displaydecoder_3_p1, displaydecoder_3_p3,
       displaydecoder_3_p4, displaydecoder_3_p6, displaydecoder_3_p7, displaydecoder_3_p9,
       displaydecoder_3_p10;

  // DisplayDecoder #(.multibit("false")) displaydecoder_1: pin names not known; wires that end beside it: displaydecoder_1_p1, A1, displaydecoder_1_p3, displaydecoder_1_p4, A2, displaydecoder_1_p6, displaydecoder_1_p7, A3, displaydecoder_1_p9, displaydecoder_1_p10, A4
  _7_Segment_Display u_7_segment_display_1 (
    .g(displaydecoder_1_p10), .f(displaydecoder_1_p9), .a(displaydecoder_1_p1), .b(displaydecoder_1_p3),
    .e(displaydecoder_1_p7), .d(displaydecoder_1_p6), .c(displaydecoder_1_p4));  // open: dp
  _74283 u_74283_1 (
    .pin1(A2___B2), .pin2(A2), .pin3(B2), .pin4(A1___B1), .pin5(A1), .pin6(B1), .pin7(Carry_In), .pin15(B3),
    .pin14(A3), .pin13(A3___B3), .pin12(B4), .pin11(A4), .pin10(A4___B4), .pin9(Carry_Out));
  _7_Segment_Display u_7_segment_display_2 (
    .g(displaydecoder_2_p10), .f(displaydecoder_2_p9), .a(displaydecoder_2_p1), .b(displaydecoder_2_p3),
    .e(displaydecoder_2_p7), .d(displaydecoder_2_p6), .c(displaydecoder_2_p4));  // open: dp
  // DisplayDecoder #(.multibit("false")) displaydecoder_2: pin names not known; wires that end beside it: displaydecoder_2_p1, B1, displaydecoder_2_p3, displaydecoder_2_p4, B2, displaydecoder_2_p6, displaydecoder_2_p7, B3, displaydecoder_2_p9, displaydecoder_2_p10, B4
  // DisplayDecoder #(.multibit("false")) displaydecoder_3: pin names not known; wires that end beside it: displaydecoder_3_p1, A1___B1, displaydecoder_3_p3, displaydecoder_3_p4, A2___B2, displaydecoder_3_p6, displaydecoder_3_p7, A3___B3, displaydecoder_3_p9, displaydecoder_3_p10, A4___B4
  _7_Segment_Display u_7_segment_display_3 (
    .g(displaydecoder_3_p10), .f(displaydecoder_3_p9), .a(displaydecoder_3_p1), .b(displaydecoder_3_p3),
    .e(displaydecoder_3_p7), .d(displaydecoder_3_p6), .c(displaydecoder_3_p4));  // open: dp

  // Notes on the sheet:
  //   Display $Valor A
  //   Display $Valor B
  //   Soma de A + B
endmodule
