// Logisim project 2 - ULA de 1 bit.circ as structural Verilog: 1 circuit, main circuit main
module main (
  input  in_1,
  input  in_2,
  output \Operação ,
  output out_4
);

  and and_1 (\Operação , in_1, in_2);
  or or_1 (out_4, in_1, in_2);
endmodule
