// Logisim project R6A1.2.circ as structural Verilog: 1 circuit, main circuit main
module main (
  input  a,
  input  b,
  input  c,
  input  d,
  output x
);

  wire and_1_out, not_1_out, not_2_out, or_1_out, or_2_out;

  not not_1 (not_1_out, c);
  not not_2 (not_2_out, b);
  or or_1 (or_1_out, not_2_out, d);
  and and_1 (and_1_out, not_1_out, or_1_out);
  or or_2 (or_2_out, b, and_1_out);
  and and_2 (x, a, or_2_out);
endmodule
