// Logisim project R6A5.1.circ as structural Verilog: 1 circuit, main circuit main
module main (
  input  D,
  input  A,
  input  C,
  input  B,
  output x
);

  wire and_1_out, or_1_out, or_2_out, or_3_out;

  or or_1 (or_1_out, D, A);
  or or_2 (or_2_out, A, C);
  or or_3 (or_3_out, C, B);
  and and_1 (and_1_out, A, B);
  // XOR_Gate xor_1 has open pins: in0=D, in1=B, out=open
  // XOR_Gate xor_2 has open pins: in0=D, in1=C, out=open
endmodule
