// Logisim project R6A5.circ as structural Verilog: 1 circuit, main circuit main
module main (
  input  D,
  input  C,
  input  B,
  input  A,
  output out_5
);

  wire and_1_out, xor_1_out, xor_2_out;

  xor xor_1 (xor_1_out, D, C);
  xor xor_2 (xor_2_out, D, B);
  and and_1 (and_1_out, B, A);
  and and_2 (out_5, xor_1_out, xor_2_out, and_1_out);
endmodule
