// Logisim project R6A6.1.circ as structural Verilog: 1 circuit, main circuit main
module main (
  input  M,
  input  F1,
  input  F2,
  input  F3,
  output x
);

  wire and_1_out, and_2_out, and_3_out, nand_1_out, nand_2_out, nand_3_out;

  nand nand_1 (nand_1_out, F2, F3);
  nand nand_2 (nand_2_out, F3, F1);
  nand nand_3 (nand_3_out, F1, F2);
  and and_1 (and_1_out, M, F1, nand_1_out);
  and and_2 (and_2_out, M, F2, nand_2_out);
  and and_3 (and_3_out, M, F3, nand_3_out);
  or or_1 (x, and_1_out, and_2_out, and_3_out);
endmodule
