// Logisim project 2 - Multiplicador FINAL.circ as structural Verilog: 1 circuit, main circuit main
module main (
  input  [3:0] A,
  input  [3:0] B,
  output [7:0] \Saída 
);

  wire displaydecoder_1_p1, displaydecoder_1_p3, displaydecoder_1_p4, displaydecoder_1_p6,
       displaydecoder_1_p7, displaydecoder_1_p9, displaydecoder_1_p10, displaydecoder_2_p1,
       displaydecoder_2_p3, displaydecoder_2_p4, displaydecoder_2_p6, displaydecoder_2_p7,
       displaydecoder_2_p9, displaydecoder_2_p10, displaydecoder_3_p1, displaydecoder_3_p2,
       displaydecoder_3_p3, displaydecoder_3_p4, displaydecoder_3_p5, displaydecoder_3_p6,
       displaydecoder_3_p7, displaydecoder_4_p1, displaydecoder_4_p2, displaydecoder_4_p3,
       displaydecoder_4_p4, displaydecoder_4_p5, displaydecoder_4_p6, displaydecoder_4_p7;
  wire [4:0] and_1_out, and_2_out, and_3_out, and_4_out;
  wire [4:1] adder_1_out, adder_2_out;
  wire [4:4] adder_1_cout, adder_2_cout;

  // DisplayDecoder #(.multibit("false")) displaydecoder_1: pin names not known; wires that end beside it: displaydecoder_1_p1, A[0], displaydecoder_1_p3, displaydecoder_1_p4, A[1], displaydecoder_1_p6, displaydecoder_1_p7, A[2], displaydecoder_1_p9, displaydecoder_1_p10, A[3]
  assign and_1_out = {5{A[0]}} & {1'b0, B};  // AND_Gate and_1, 5 bits wide
  _7_Segment_Display u_7_segment_display_1 (
    .g(displaydecoder_1_p10), .f(displaydecoder_1_p9), .a(displaydecoder_1_p1), .b(displaydecoder_1_p3),
    .e(displaydecoder_1_p7), .d(displaydecoder_1_p6), .c(displaydecoder_1_p4));  // open: dp
  assign and_2_out = {B, 1'b0} & {5{A[1]}};  // AND_Gate and_2, 5 bits wide
  Adder #(.width(5)) adder_1 (
    .a(and_2_out), .b(and_1_out), .out({adder_1_out, \Saída [0]}), .cout(adder_1_cout[4]));  // open: cin
  assign and_3_out = {5{A[2]}} & {B, 1'b0};  // AND_Gate and_3, 5 bits wide
  assign and_4_out = {5{A[3]}} & {B, 1'b0};  // AND_Gate and_4, 5 bits wide
  Adder #(.width(5)) adder_2 (
    .a(and_3_out), .b({adder_1_cout[4], adder_1_out}), .out({adder_2_out, \Saída [1]}), .cout(adder_2_cout[4]));  // open: cin
  // DisplayDecoder #(.multibit("false")) displaydecoder_2: pin names not known; wires that end beside it: displaydecoder_2_p1, B[0], displaydecoder_2_p3, displaydecoder_2_p4, B[1], displaydecoder_2_p6, displaydecoder_2_p7, B[2], displaydecoder_2_p9, displaydecoder_2_p10, B[3]
  _7_Segment_Display u_7_segment_display_2 (
    .g(displaydecoder_2_p10), .f(displaydecoder_2_p9), .a(displaydecoder_2_p1), .b(displaydecoder_2_p3),
    .e(displaydecoder_2_p7), .d(displaydecoder_2_p6), .c(displaydecoder_2_p4));  // open: dp
  Adder #(.width(5)) adder_3 (
    .a(and_4_out), .b({adder_2_cout[4], adder_2_out}), .out(\Saída [6:2]), .cout(\Saída [7]));  // open: cin
  // DisplayDecoder #(.multibit("false")) displaydecoder_3: pin names not known; wires that end beside it: displaydecoder_3_p1, displaydecoder_3_p2, displaydecoder_3_p3, displaydecoder_3_p4, displaydecoder_3_p5, displaydecoder_3_p6, displaydecoder_3_p7
  _7_Segment_Display u_7_segment_display_3 (
    .g(displaydecoder_3_p7), .f(displaydecoder_3_p6), .a(displaydecoder_3_p1), .b(displaydecoder_3_p2),
    .e(displaydecoder_3_p5), .d(displaydecoder_3_p4), .c(displaydecoder_3_p3));  // open: dp
  // DisplayDecoder #(.multibit("false")) displaydecoder_4: pin names not known; wires that end beside it: displaydecoder_4_p1, displaydecoder_4_p2, displaydecoder_4_p3, displaydecoder_4_p4, displaydecoder_4_p5, displaydecoder_4_p6, displaydecoder_4_p7
  _7_Segment_Display u_7_segment_display_4 (
    .g(displaydecoder_4_p7), .f(displaydecoder_4_p6), .a(displaydecoder_4_p1), .b(displaydecoder_4_p2),
    .e(displaydecoder_4_p5), .d(displaydecoder_4_p4), .c(displaydecoder_4_p3));  // open: dp

  // Notes on the sheet:
  //   Display $Valor A
  //   Display $Valor B
  //   Display $Valor A
  //   Display $Valor A
endmodule
