// Logisim project R5A4.circ as structural Verilog: 1 circuit, main circuit main
module main (
  input  Fogo,
  input  Energia,
  input  Gas,
  output out_4
);

  wire and_1_out;

  and and_1 (and_1_out, Energia, Gas);
  or or_1 (out_4, Fogo, and_1_out);
endmodule
