// Logisim project R5A3 - Avaliando Todos os Teoremas Booleanos Fundamentais.circ as structural Verilog: 1 circuit, main circuit main
module main (
  input  in_1,
  input  in_2,
  input  in_3,
  input  in_4,
  input  in_5,
  input  in_6,
  input  in_7,
  input  in_8,
  input  in_9,
  input  in_10,
  input  in_11,
  input  in_12,
  output out_13,
  output out_14,
  output out_15,
  output out_16,
  output out_17,
  output out_18,
  output out_19,
  output out_20,
  output out_21,
  output out_22
);

  wire and_3_out, and_6_out, and_7_out, not_1_out, not_2_out, not_3_out;

  or or_1 (out_14, in_2, 1'b0);
  or or_2 (out_16, in_4, in_4);
  and and_1 (out_18, in_6, 1'b0);
  and and_2 (out_20, in_8, in_8);
  and and_3 (and_3_out, in_9, in_12);
  or or_3 (out_21, in_9, and_3_out);
  or or_4 (out_13, in_1, 1'b1);
  not not_1 (not_1_out, in_3);
  and and_4 (out_17, in_5, 1'b1);
  not not_2 (not_2_out, in_7);
  not not_3 (not_3_out, in_11);
  or or_5 (out_15, in_3, not_1_out);
  and and_5 (out_19, in_7, not_2_out);
  and and_6 (and_6_out, in_10, in_11);
  and and_7 (and_7_out, not_3_out, in_10);
  or or_6 (out_22, and_6_out, and_7_out);
endmodule
