// Logisim project R5A5.circ as structural Verilog: 1 circuit, main circuit main
module main (
  input  _40,
  input  _30,
  input  _30_2,
  output Aprovado
);

  wire or_1_out;

  or or_1 (or_1_out, _30, _30_2);
  and and_1 (Aprovado, _40, or_1_out);
endmodule
