// Logisim project R6A1.1.circ as structural Verilog: 1 circuit, main circuit main
module main (
  input  a,
  input  b,
  input  c,
  output x
);

  wire not_1_out, not_2_out, or_1_out, or_2_out;

  not not_1 (not_1_out, b);
  not not_2 (not_2_out, c);
  or or_1 (or_1_out, not_1_out, not_2_out);
  or or_2 (or_2_out, b, c);
  and and_1 (x, a, or_1_out, or_2_out);
endmodule
