// Logisim project R6A2.1.circ as structural Verilog: 1 circuit, main circuit main
module main (
  input  a,
  input  b,
  output x
);

  wire and_1_out, not_1_out, not_2_out, not_3_out, or_1_out, or_2_out;

  not not_1 (not_1_out, b);
  and and_1 (and_1_out, a, b);
  not not_2 (not_2_out, b);
  or or_1 (or_1_out, a, not_1_out, and_1_out);
  or or_2 (or_2_out, a, not_2_out);
  not not_3 (not_3_out, a);
  and and_2 (x, or_1_out, or_2_out, not_3_out, b);
endmodule
