// Logisim project R6A2.3.circ as structural Verilog: 1 circuit, main circuit main
module main (
  input  a,
  input  b,
  input  c,
  input  d,
  output x
);

  wire and_1_out, nand_1_out, not_1_out, not_2_out, or_1_out;

  not not_1 (not_1_out, b);
  or or_1 (or_1_out, not_1_out, not_2_out);
  not not_2 (not_2_out, c);
  and and_1 (and_1_out, or_1_out, a);
  nand nand_1 (nand_1_out, c, d);
  nor nor_1 (x, and_1_out, nand_1_out);
endmodule
