// Logisim project R6A3.circ as structural Verilog: 1 circuit, main circuit main
module main (
  input  A,
  input  B,
  input  C,
  input  D,
  output x
);

  wire and_1_out, and_2_out, nand_1_out, nand_2_out, or_1_out;

  and and_1 (and_1_out, B, C);
  and and_2 (and_2_out, C, D);
  nand nand_1 (nand_1_out, A, B, C);
  and and_3 (x, nand_1_out, nand_2_out, or_1_out);
  nand nand_2 (nand_2_out, A, C, D);
  or or_1 (or_1_out, and_1_out, and_2_out);
endmodule
