// Logisim project R6A4.circ as structural Verilog: 1 circuit, main circuit main
module main (
  input  Temperatura,
  input  \Pressão ,
  input  RPM,
  output Aviso
);

  wire or_1_out;

  or or_1 (or_1_out, RPM, \Pressão );
  and and_1 (Aviso, Temperatura, or_1_out);
endmodule
